// Logisim project 24-bit-ALU(VERS2).circ as structural Verilog: 19 circuits, main circuit main cpu
module main_cpu (
);

  wire clock_1_out, cpu_1_r, cpu_1_w, Reset_out;
  wire [7:0] cpu_1_addr;
  wire [23:0] cpu_1_dataout, ram_1_data;

  Clock clock_1 (.out(clock_1_out));
  Button Reset (.out(Reset_out));
  CPU cpu_1 (
    .Reset(Reset_out), .Clk(clock_1_out), .DataIn(ram_1_data), .DataOut(cpu_1_dataout), .R(cpu_1_r),
    .Addr(cpu_1_addr), .w(cpu_1_w));
  RAM #(.dataWidth(24), .bus("separate")) ram_1 (
    .addr(cpu_1_addr), .din(cpu_1_dataout), .data(ram_1_data), .str(cpu_1_w), .clk(clock_1_out), .ld(cpu_1_r));  // open: sel, clr

  // Notes on the sheet:
  //   0 - AND
  //   1 - OR
  //   8-DEC
  //   2 - STO
  //   9-RT LEFT
  //   3 - ADD
  //   4 - SUB
  //   10-RT RIght
  //   5 - BUN
  //   11-JC
  //   6 - LDA
  //   12-JNC
  //   7 - INC
  //   13. Booths
  //   OPCODE(4BIT)|ADDERESS(8BIT)|EMPTY(12BIT)
endmodule

module CPU (
  input  Reset,
  input  Clk,
  input  [23:0] DataIn,
  output w,
  output [23:0] DataOut,
  output R,
  output [7:0] Addr
);

  wire A_to_B, and_2_out, and_3_out, B_AD__to_MAR, Booths_p5, Busy, C0, C1, C2, CF, demultiplexer_1_out0,
       INC_PC, JNCF, JNF, JNNF, LdAfrB, LoadAC, LoadAc_t, LoadB, LoadMAR, MBR_to_PC, mul_flag, NF, not_1_out,
       OF, or_4_out, PC_to_MAR, ZF;
  wire [3:0] main_1_zero;
  wire [7:0] multiplexer_3_out, PC_OUT;
  wire [23:0] A, AC, AcIn, ALUout, multiplexer_2_out, Q;

  Demultiplexer #(.enable("false")) demultiplexer_1 (.out0(demultiplexer_1_out0), .in(Clk), .sel(Busy));  // open: out1
  Multiplexer #(.width(24), .enable("false")) multiplexer_1 (.in0(ALUout), .in1(DataOut), .out(AcIn), .sel(LdAfrB));
  ControlUnit controlunit_1 (
    .IR(DataOut[23:20]), .clk(demultiplexer_1_out0), .Reset(Reset), .PC_to_MAR(PC_to_MAR), .INC_PC(INC_PC),
    .Memory_to_MBR(R), .MBR_AD__to_PC(MBR_to_PC), .B_AD__to_MAR(B_AD__to_MAR), .LoadAc(LoadAC), .JCF(JNF),
    .JNCF(JNNF), .AtoB(A_to_B), .MBR_to_Memory(w), .LdAfrB(LdAfrB), .Operation({C2, C1, C0}), .mf(mul_flag));
  Multiplexer #(.width(24), .enable("false")) multiplexer_2 (
    .in0(DataIn), .in1(AC), .out(multiplexer_2_out), .sel(A_to_B));
  Register #(.width(24)) MUL_OUTPUT_1 (.D(Q), .en(mul_flag), .clk(Clk), .clr(Reset));  // open: Q
  Multiplexer #(.width(8), .enable("false")) multiplexer_3 (
    .in0(PC_OUT), .in1(DataOut[19:12]), .out(multiplexer_3_out), .sel(B_AD__to_MAR));
  Register #(.width(24)) MBR (.D(multiplexer_2_out), .en(LoadB), .Q(DataOut), .clk(Clk), .clr(Reset));
  Register MAR (.D(multiplexer_3_out), .en(LoadMAR), .Q(Addr), .clk(Clk), .clr(Reset));
  or or_1 (LoadMAR, PC_to_MAR, B_AD__to_MAR);
  Register #(.width(24)) MUL_OUTPUT_2 (.D(A), .en(mul_flag), .clk(Clk), .clr(Reset));  // open: Q
  or or_2 (LoadAc_t, LdAfrB, LoadAC);
  Register #(.width(24)) u_Ac (.D(AcIn), .en(LoadAc_t), .Q(AC), .clk(Clk), .clr(Reset));
  // Booth_s_multiplier Booths: pin names not known; wires that end beside it: AC, DataOut, Reset, Busy, Booths_p5, Q, A
  and and_1 (Booths_p5, Clk, mul_flag);
  or or_3 (LoadB, R, A_to_B);
  main main_1 (
    .C1(C1), .C0(C0), .A(AC), .B(DataOut), .Result(ALUout), .Zero(main_1_zero[0]), .Negative(main_1_zero[1]),
    .Overflow(main_1_zero[2]), .Carry(main_1_zero[3]), .C2(C2));
  Register #(.width(4)) IR (.D(DataOut[23:20]), .en(INC_PC), .clk(Clk), .clr(Reset));  // open: Q
  and and_2 (and_2_out, NF, JNF);
  and and_3 (and_3_out, JNCF, not_1_out);
  not not_1 (not_1_out, JNNF);
  Register #(.width(4)) register_1 (.D(main_1_zero), .en(LoadAC), .Q({CF, OF, NF, ZF}), .clk(Clk));  // open: clr
  or or_4 (or_4_out, MBR_to_PC, and_2_out, and_3_out);
  Counter PC (.load(or_4_out), .D(DataOut[19:12]), .count(INC_PC), .Q(PC_OUT), .clk(Clk), .clr(Reset));  // open: carry

  // Other names for the same wires on the sheet: clr = Reset; MBR_to_Memory = w; MBRout[23:0] = DataOut;
  //   MBR_ADD[7:0] = DataOut[19:12]; OPCODE[3:0] = DataOut[23:20]; Memory_to_MBR = R
endmodule

module ControlUnit (
  input  [3:0] IR,
  input  clk,
  input  Reset,
  output PC_to_MAR,
  output INC_PC,
  output Memory_to_MBR,
  output MBR_AD__to_PC,
  output B_AD__to_MAR,
  output [2:0] Operation,
  output LoadAc,
  output mf,
  output JCF,
  output JNCF,
  output AtoB,
  output MBR_to_Memory,
  output LdAfrB
);

  wire and_1_out, decoder_1_out6, decoder_1_out7, decoder_1_out8, decoder_1_out9, decoder_1_out15,
       decoder_1_out16, decoder_1_out17, decoder_1_out18, decoder_1_out31, not_1_out, or_1_out;
  wire [5:0] counter_1_q;
  wire [7:0] rom_1_data;

  Counter #(.width(6), .max('h3f)) counter_1 (
    .load(rom_1_data[2]), .D({IR, 2'b11}), .count(rom_1_data[0]), .Q(counter_1_q), .clk(and_1_out),
    .clr(or_1_out));  // open: carry
  or or_1 (or_1_out, rom_1_data[1], Reset);
  and and_1 (and_1_out, clk, not_1_out);
  ROM #(.addrWidth(6)) rom_1 (.addr(counter_1_q), .data(rom_1_data));  // open: sel
  not not_1 (not_1_out, decoder_1_out31);
  Decoder #(.select(5), .enable("false")) decoder_1 (
    .out1(PC_to_MAR), .out2(INC_PC), .out3(Memory_to_MBR), .out4(MBR_AD__to_PC), .out5(B_AD__to_MAR),
    .out6(decoder_1_out6), .out7(decoder_1_out7), .out8(decoder_1_out8), .out9(decoder_1_out9), .out10(AtoB),
    .out11(MBR_to_Memory), .out14(LdAfrB), .out15(decoder_1_out15), .out16(decoder_1_out16),
    .out17(decoder_1_out17), .out18(decoder_1_out18), .out19(JCF), .out20(JNCF), .out25(mf),
    .out31(decoder_1_out31), .sel(rom_1_data[7:3]));  // open: out0, out12, out13, out21, out22, out23, out24, out26, out27, out28, out29, out30
  Priority_Encoder priority_encoder_1 (
    .in0(decoder_1_out6), .in1(decoder_1_out7), .in2(decoder_1_out8), .in3(decoder_1_out9),
    .in4(decoder_1_out15), .in5(decoder_1_out16), .in6(decoder_1_out17), .in7(decoder_1_out18),
    .out(Operation));  // open: en_in, gs, en_out
  or or_2 (LoadAc, decoder_1_out6, decoder_1_out7, decoder_1_out8, decoder_1_out9, decoder_1_out15, decoder_1_out16, decoder_1_out17, decoder_1_out18);

  // Notes on the sheet:
  //   contents of rom_1 (hex, n*v repeats v):
  //   9 19 14 29 19 31 2 29 19 39 2 29 51 59 2 29 19 41 2 29 19 49 2 21 2 2 2 29 19 71 2 79 2 2 2 81 2 2 2
  //   89 2 2 2 91 2 2 2 99 2 2 2 a1 2 2 2 29 19 c9 c9 c9 2 0 0 f9
endmodule

// ALU
module main (
  input  C2,
  input  C1,
  input  C0,
  input  [23:0] A,
  input  [23:0] B,
  output [23:0] Result,
  output Zero,
  output Negative,
  output Overflow,
  output Carry
);

  _24_bit_ALU u_24_bit_alu_1 (
    .A(A), .B(B), .Result(Result), .Zero(Zero), .Negative(Negative), .Overflow(Overflow), .Control0(C0),
    .Control1(C1), .Control2(C2), .Carry(Carry));
endmodule

// 24-bit AND
module _24_bit_and (
  input  [23:0] A,
  input  [23:0] B,
  output [23:0] Result
);

  and and_1 (Result[0], A[0], B[0]);
  and and_2 (Result[1], A[1], B[1]);
  and and_3 (Result[2], A[2], B[2]);
  and and_4 (Result[3], A[3], B[3]);
  and and_5 (Result[4], A[4], B[4]);
  and and_6 (Result[5], A[5], B[5]);
  and and_7 (Result[6], A[6], B[6]);
  and and_8 (Result[7], A[7], B[7]);
  and and_9 (Result[8], A[8], B[8]);
  and and_10 (Result[9], A[9], B[9]);
  and and_11 (Result[10], A[10], B[10]);
  and and_12 (Result[11], A[11], B[11]);
  and and_13 (Result[12], A[12], B[12]);
  and and_14 (Result[13], A[13], B[13]);
  and and_15 (Result[14], A[14], B[14]);
  and and_16 (Result[15], A[15], B[15]);
  and and_17 (Result[16], A[16], B[16]);
  and and_18 (Result[17], A[17], B[17]);
  and and_19 (Result[18], A[18], B[18]);
  and and_20 (Result[19], A[19], B[19]);
  and and_21 (Result[20], A[20], B[20]);
  and and_22 (Result[21], A[21], B[21]);
  and and_23 (Result[22], A[22], B[22]);
  and and_24 (Result[23], A[23], B[23]);
endmodule

// 24-bit OR
module _24_bit_OR (
  input  [23:0] A,
  input  [23:0] B,
  output [23:0] Result
);

  or or_1 (Result[0], A[0], B[0]);
  or or_2 (Result[1], A[1], B[1]);
  or or_3 (Result[2], A[2], B[2]);
  or or_4 (Result[3], A[3], B[3]);
  or or_5 (Result[4], A[4], B[4]);
  or or_6 (Result[5], A[5], B[5]);
  or or_7 (Result[6], A[6], B[6]);
  or or_8 (Result[7], A[7], B[7]);
  or or_9 (Result[8], A[8], B[8]);
  or or_10 (Result[9], A[9], B[9]);
  or or_11 (Result[10], A[10], B[10]);
  or or_12 (Result[11], A[11], B[11]);
  or or_13 (Result[12], A[12], B[12]);
  or or_14 (Result[13], A[13], B[13]);
  or or_15 (Result[14], A[14], B[14]);
  or or_16 (Result[15], A[15], B[15]);
  or or_17 (Result[16], A[16], B[16]);
  or or_18 (Result[17], A[17], B[17]);
  or or_19 (Result[18], A[18], B[18]);
  or or_20 (Result[19], A[19], B[19]);
  or or_21 (Result[20], A[20], B[20]);
  or or_22 (Result[21], A[21], B[21]);
  or or_23 (Result[22], A[22], B[22]);
  or or_24 (Result[23], A[23], B[23]);
endmodule

module Full_adder (
  input  Carry_in,
  input  A,
  input  B,
  output Result,
  output Carry_out
);

  wire and_1_out, and_2_out, xor_1_out;

  and and_1 (and_1_out, B, A);
  xor xor_1 (xor_1_out, A, B);
  or or_1 (Carry_out, and_1_out, and_2_out);
  and and_2 (and_2_out, xor_1_out, Carry_in);
  xor xor_2 (Result, Carry_in, xor_1_out);
endmodule

module _24_bit_full_adder (
  input  Carry_in,
  input  A0,
  input  B0,
  input  A1,
  input  B1,
  input  A2,
  input  B2,
  input  A3,
  input  B3,
  input  A4,
  input  B4,
  input  A5,
  input  B5,
  input  A6,
  input  B6,
  input  A7,
  input  B7,
  input  A8,
  input  B8,
  input  A9,
  input  B9,
  input  A10,
  input  B10,
  input  A11,
  input  B11,
  input  A12,
  input  B12,
  input  A13,
  input  B13,
  input  A14,
  input  B14,
  input  A15,
  input  B15,
  input  A16,
  input  B16,
  input  A17,
  input  B17,
  input  A18,
  input  B18,
  input  A19,
  input  B19,
  input  A20,
  input  B20,
  input  A21,
  input  B21,
  input  A22,
  input  B22,
  input  A23,
  input  B23,
  input  A24,
  input  B24,
  input  A25,
  input  B25,
  input  A26,
  input  B26,
  input  A27,
  input  B27,
  input  A28,
  input  B28,
  input  A29,
  input  B29,
  input  A30,
  input  B30,
  input  A31,
  input  B31,
  output Result0,
  output Result1,
  output Result2,
  output Result3,
  output Result4,
  output Result5,
  output Result6,
  output Result7,
  output Result8,
  output Result9,
  output Result10,
  output Result11,
  output Result12,
  output Result13,
  output Result14,
  output Result15,
  output Result16,
  output Result17,
  output Result18,
  output Result19,
  output Result20,
  output Result21,
  output Result22,
  output Result23,
  output Result24,
  output Result25,
  output Result26,
  output Result27,
  output Result28,
  output Result29,
  output Result30,
  output Result31,
  output Carry
);

  wire full_adder_1_carry_out, full_adder_2_carry_out, full_adder_3_carry_out, full_adder_4_carry_out,
       full_adder_5_carry_out, full_adder_6_carry_out, full_adder_7_carry_out, full_adder_8_carry_out,
       full_adder_9_carry_out, full_adder_10_carry_out, full_adder_11_carry_out, full_adder_12_carry_out,
       full_adder_13_carry_out, full_adder_14_carry_out, full_adder_15_carry_out, full_adder_16_carry_out,
       full_adder_17_carry_out, full_adder_18_carry_out, full_adder_19_carry_out, full_adder_20_carry_out,
       full_adder_21_carry_out, full_adder_22_carry_out, full_adder_23_carry_out, full_adder_24_carry_out,
       full_adder_25_carry_out, full_adder_26_carry_out, full_adder_27_carry_out, full_adder_28_carry_out,
       full_adder_29_carry_out, full_adder_30_carry_out, full_adder_31_carry_out;

  Full_adder full_adder_1 (.Carry_in(Carry_in), .A(A0), .B(B0), .Result(Result0), .Carry_out(full_adder_1_carry_out));
  Full_adder full_adder_2 (
    .Carry_in(full_adder_1_carry_out), .A(A1), .B(B1), .Result(Result1), .Carry_out(full_adder_2_carry_out));
  Full_adder full_adder_3 (
    .Carry_in(full_adder_2_carry_out), .A(A2), .B(B2), .Result(Result2), .Carry_out(full_adder_3_carry_out));
  Full_adder full_adder_4 (
    .Carry_in(full_adder_3_carry_out), .A(A3), .B(B3), .Result(Result3), .Carry_out(full_adder_4_carry_out));
  Full_adder full_adder_5 (
    .Carry_in(full_adder_4_carry_out), .A(A4), .B(B4), .Result(Result4), .Carry_out(full_adder_5_carry_out));
  Full_adder full_adder_6 (
    .Carry_in(full_adder_5_carry_out), .A(A5), .B(B5), .Result(Result5), .Carry_out(full_adder_6_carry_out));
  Full_adder full_adder_7 (
    .Carry_in(full_adder_6_carry_out), .A(A6), .B(B6), .Result(Result6), .Carry_out(full_adder_7_carry_out));
  Full_adder full_adder_8 (
    .Carry_in(full_adder_7_carry_out), .A(A7), .B(B7), .Result(Result7), .Carry_out(full_adder_8_carry_out));
  Full_adder full_adder_9 (
    .Carry_in(full_adder_8_carry_out), .A(A8), .B(B8), .Result(Result8), .Carry_out(full_adder_9_carry_out));
  Full_adder full_adder_10 (
    .Carry_in(full_adder_9_carry_out), .A(A9), .B(B9), .Result(Result9), .Carry_out(full_adder_10_carry_out));
  Full_adder full_adder_11 (
    .Carry_in(full_adder_10_carry_out), .A(A10), .B(B10), .Result(Result10),
    .Carry_out(full_adder_11_carry_out));
  Full_adder full_adder_12 (
    .Carry_in(full_adder_11_carry_out), .A(A11), .B(B11), .Result(Result11),
    .Carry_out(full_adder_12_carry_out));
  Full_adder full_adder_13 (
    .Carry_in(full_adder_12_carry_out), .A(A12), .B(B12), .Result(Result12),
    .Carry_out(full_adder_13_carry_out));
  Full_adder full_adder_14 (
    .Carry_in(full_adder_13_carry_out), .A(A13), .B(B13), .Result(Result13),
    .Carry_out(full_adder_14_carry_out));
  Full_adder full_adder_15 (
    .Carry_in(full_adder_14_carry_out), .A(A14), .B(B14), .Result(Result14),
    .Carry_out(full_adder_15_carry_out));
  Full_adder full_adder_16 (
    .Carry_in(full_adder_15_carry_out), .A(A15), .B(B15), .Result(Result15),
    .Carry_out(full_adder_16_carry_out));
  Full_adder full_adder_17 (
    .Carry_in(full_adder_16_carry_out), .A(A16), .B(B16), .Result(Result16),
    .Carry_out(full_adder_17_carry_out));
  Full_adder full_adder_18 (
    .Carry_in(full_adder_17_carry_out), .A(A17), .B(B17), .Result(Result17),
    .Carry_out(full_adder_18_carry_out));
  Full_adder full_adder_19 (
    .Carry_in(full_adder_18_carry_out), .A(A18), .B(B18), .Result(Result18),
    .Carry_out(full_adder_19_carry_out));
  Full_adder full_adder_20 (
    .Carry_in(full_adder_19_carry_out), .A(A19), .B(B19), .Result(Result19),
    .Carry_out(full_adder_20_carry_out));
  Full_adder full_adder_21 (
    .Carry_in(full_adder_20_carry_out), .A(A20), .B(B20), .Result(Result20),
    .Carry_out(full_adder_21_carry_out));
  Full_adder full_adder_22 (
    .Carry_in(full_adder_21_carry_out), .A(A21), .B(B21), .Result(Result21),
    .Carry_out(full_adder_22_carry_out));
  Full_adder full_adder_23 (
    .Carry_in(full_adder_22_carry_out), .A(A22), .B(B22), .Result(Result22),
    .Carry_out(full_adder_23_carry_out));
  Full_adder full_adder_24 (
    .Carry_in(full_adder_23_carry_out), .A(A23), .B(B23), .Result(Result23),
    .Carry_out(full_adder_24_carry_out));
  Full_adder full_adder_25 (
    .Carry_in(full_adder_24_carry_out), .A(A24), .B(B24), .Result(Result24),
    .Carry_out(full_adder_25_carry_out));
  Full_adder full_adder_26 (
    .Carry_in(full_adder_25_carry_out), .A(A25), .B(B25), .Result(Result25),
    .Carry_out(full_adder_26_carry_out));
  Full_adder full_adder_27 (
    .Carry_in(full_adder_26_carry_out), .A(A26), .B(B26), .Result(Result26),
    .Carry_out(full_adder_27_carry_out));
  Full_adder full_adder_28 (
    .Carry_in(full_adder_27_carry_out), .A(A27), .B(B27), .Result(Result27),
    .Carry_out(full_adder_28_carry_out));
  Full_adder full_adder_29 (
    .Carry_in(full_adder_28_carry_out), .A(A28), .B(B28), .Result(Result28),
    .Carry_out(full_adder_29_carry_out));
  Full_adder full_adder_30 (
    .Carry_in(full_adder_29_carry_out), .A(A29), .B(B29), .Result(Result29),
    .Carry_out(full_adder_30_carry_out));
  Full_adder full_adder_31 (
    .Carry_in(full_adder_30_carry_out), .A(A30), .B(B30), .Result(Result30),
    .Carry_out(full_adder_31_carry_out));
  Full_adder full_adder_32 (.Carry_in(full_adder_31_carry_out), .A(A31), .B(B31), .Result(Result31), .Carry_out(Carry));
endmodule

// FA
module _24_bit_full_adder_concise (
  input  Carry_in,
  input  [23:0] A,
  input  [23:0] B,
  output [23:0] Result,
  output Carry
);

  wire full_adder_1_carry_out, full_adder_2_carry_out, full_adder_3_carry_out, full_adder_4_carry_out,
       full_adder_5_carry_out, full_adder_6_carry_out, full_adder_7_carry_out, full_adder_8_carry_out,
       full_adder_9_carry_out, full_adder_10_carry_out, full_adder_11_carry_out, full_adder_12_carry_out,
       full_adder_13_carry_out, full_adder_14_carry_out, full_adder_15_carry_out, full_adder_16_carry_out,
       full_adder_17_carry_out, full_adder_18_carry_out, full_adder_19_carry_out, full_adder_20_carry_out,
       full_adder_21_carry_out, full_adder_22_carry_out, full_adder_23_carry_out;

  Full_adder full_adder_1 (
    .Carry_in(Carry_in), .A(A[0]), .B(B[0]), .Result(Result[0]), .Carry_out(full_adder_1_carry_out));
  Full_adder full_adder_2 (
    .Carry_in(full_adder_1_carry_out), .A(A[1]), .B(B[1]), .Result(Result[1]),
    .Carry_out(full_adder_2_carry_out));
  Full_adder full_adder_3 (
    .Carry_in(full_adder_2_carry_out), .A(A[2]), .B(B[2]), .Result(Result[2]),
    .Carry_out(full_adder_3_carry_out));
  Full_adder full_adder_4 (
    .Carry_in(full_adder_3_carry_out), .A(A[3]), .B(B[3]), .Result(Result[3]),
    .Carry_out(full_adder_4_carry_out));
  Full_adder full_adder_5 (
    .Carry_in(full_adder_4_carry_out), .A(A[4]), .B(B[4]), .Result(Result[4]),
    .Carry_out(full_adder_5_carry_out));
  Full_adder full_adder_6 (
    .Carry_in(full_adder_5_carry_out), .A(A[5]), .B(B[5]), .Result(Result[5]),
    .Carry_out(full_adder_6_carry_out));
  Full_adder full_adder_7 (
    .Carry_in(full_adder_6_carry_out), .A(A[6]), .B(B[6]), .Result(Result[6]),
    .Carry_out(full_adder_7_carry_out));
  Full_adder full_adder_8 (
    .Carry_in(full_adder_7_carry_out), .A(A[7]), .B(B[7]), .Result(Result[7]),
    .Carry_out(full_adder_8_carry_out));
  Full_adder full_adder_9 (
    .Carry_in(full_adder_8_carry_out), .A(A[8]), .B(B[8]), .Result(Result[8]),
    .Carry_out(full_adder_9_carry_out));
  Full_adder full_adder_10 (
    .Carry_in(full_adder_9_carry_out), .A(A[9]), .B(B[9]), .Result(Result[9]),
    .Carry_out(full_adder_10_carry_out));
  Full_adder full_adder_11 (
    .Carry_in(full_adder_10_carry_out), .A(A[10]), .B(B[10]), .Result(Result[10]),
    .Carry_out(full_adder_11_carry_out));
  Full_adder full_adder_12 (
    .Carry_in(full_adder_11_carry_out), .A(A[11]), .B(B[11]), .Result(Result[11]),
    .Carry_out(full_adder_12_carry_out));
  Full_adder full_adder_13 (
    .Carry_in(full_adder_12_carry_out), .A(A[12]), .B(B[12]), .Result(Result[12]),
    .Carry_out(full_adder_13_carry_out));
  Full_adder full_adder_14 (
    .Carry_in(full_adder_13_carry_out), .A(A[13]), .B(B[13]), .Result(Result[13]),
    .Carry_out(full_adder_14_carry_out));
  Full_adder full_adder_15 (
    .Carry_in(full_adder_14_carry_out), .A(A[14]), .B(B[14]), .Result(Result[14]),
    .Carry_out(full_adder_15_carry_out));
  Full_adder full_adder_16 (
    .Carry_in(full_adder_15_carry_out), .A(A[15]), .B(B[15]), .Result(Result[15]),
    .Carry_out(full_adder_16_carry_out));
  Full_adder full_adder_17 (
    .Carry_in(full_adder_16_carry_out), .A(A[16]), .B(B[16]), .Result(Result[16]),
    .Carry_out(full_adder_17_carry_out));
  Full_adder full_adder_18 (
    .Carry_in(full_adder_17_carry_out), .A(A[17]), .B(B[17]), .Result(Result[17]),
    .Carry_out(full_adder_18_carry_out));
  Full_adder full_adder_19 (
    .Carry_in(full_adder_18_carry_out), .A(A[18]), .B(B[18]), .Result(Result[18]),
    .Carry_out(full_adder_19_carry_out));
  Full_adder full_adder_20 (
    .Carry_in(full_adder_19_carry_out), .A(A[19]), .B(B[19]), .Result(Result[19]),
    .Carry_out(full_adder_20_carry_out));
  Full_adder full_adder_21 (
    .Carry_in(full_adder_20_carry_out), .A(A[20]), .B(B[20]), .Result(Result[20]),
    .Carry_out(full_adder_21_carry_out));
  Full_adder full_adder_22 (
    .Carry_in(full_adder_21_carry_out), .A(A[21]), .B(B[21]), .Result(Result[21]),
    .Carry_out(full_adder_22_carry_out));
  Full_adder full_adder_23 (
    .Carry_in(full_adder_22_carry_out), .A(A[22]), .B(B[22]), .Result(Result[22]),
    .Carry_out(full_adder_23_carry_out));
  Full_adder full_adder_24 (
    .Carry_in(full_adder_23_carry_out), .A(A[23]), .B(B[23]), .Result(Result[23]), .Carry_out(Carry));
endmodule

module _24_bit_xor (
  input  Control,
  input  [23:0] B,
  output [23:0] Result
);

  wire [23:0] bit_extender_1_out;

  assign bit_extender_1_out = {{23{Control}}, Control};  // Bit_Extender bit_extender_1
  assign Result = bit_extender_1_out ^ B;  // XOR_Gate xor_1, 24 bits wide
endmodule

// 24-bit \nADD/SUB
module Add_sub (
  input  Sub,
  input  [23:0] A,
  input  [23:0] B,
  output [23:0] Result,
  output Carry,
  output Overflow
);

  wire and_1_out, and_2_out, n23th_bit_out_1__23th_bit, n23th_bit_out_2__23th_bit, n23th_bit_out_3__23th_bit,
       not_1_out, not_2_out, not_3_out;
  wire [23:0] n24_bit_xor_1_result;

  _23th_bit_out u_23th_bit_out_1 (.Input(A), ._23th_bit(n23th_bit_out_1__23th_bit));
  not not_1 (not_1_out, n23th_bit_out_1__23th_bit);
  _23th_bit_out u_23th_bit_out_2 (.Input(B), ._23th_bit(n23th_bit_out_2__23th_bit));
  not not_2 (not_2_out, n23th_bit_out_2__23th_bit);
  _24_bit_xor u_24_bit_xor_1 (.B(B), .Result(n24_bit_xor_1_result), .Control(Sub));
  _24_bit_full_adder_concise u_24_bit_full_adder_concise_1 (
    .A(A), .Result(Result), .Carry_in(Sub), .B(n24_bit_xor_1_result), .Carry(Carry));
  _23th_bit_out u_23th_bit_out_3 (.Input(Result), ._23th_bit(n23th_bit_out_3__23th_bit));
  not not_3 (not_3_out, n23th_bit_out_3__23th_bit);
  and and_1 (and_1_out, not_3_out, n23th_bit_out_2__23th_bit, n23th_bit_out_1__23th_bit);
  and and_2 (and_2_out, n23th_bit_out_3__23th_bit, not_2_out, not_1_out);
  or or_1 (Overflow, and_1_out, and_2_out);

  // Notes on the sheet:
  //   A31
  //   B31
  //   Result 31
endmodule

// 23th
module _23th_bit_out (
  input  [23:0] Input,
  output _23th_bit
);


  assign _23th_bit = Input[23];
endmodule

// Reduce-OR
module _24_bit_reduce_or (
  input  [23:0] Input,
  output Output
);

  or or_1 (Output, Input[11], Input[0], Input[1], Input[2], Input[3], Input[4], Input[5], Input[6], Input[7], Input[8], Input[9], Input[10], Input[12], Input[13], Input[14], Input[15], Input[16], Input[17], Input[18], Input[19], Input[20], Input[21], Input[22], Input[23]);
endmodule

module _24_bit_ALU (
  input  Control0,
  input  Control2,
  input  Control1,
  input  [23:0] A,
  input  [23:0] B,
  output [23:0] Result,
  output Zero,
  output Negative,
  output Overflow,
  output Carry
);

  wire add_sub_1_carry, add_sub_1_overflow, inc_dec_1_carry, inc_dec_1_overflow, n24_bit_reduce_or_1_output;
  wire [23:0] add_sub_1_result, inc_dec_1_result, n24_bit_and_or_1_result, rotate_left_right_1_result;

  _24_bit_and_or u_24_bit_and_or_1 (.A(A), .B(B), .Result(n24_bit_and_or_1_result), .in_3(Control0));
  Add_sub add_sub_1 (
    .Sub(Control0), .A(A), .B(B), .Result(add_sub_1_result), .Carry(add_sub_1_carry),
    .Overflow(add_sub_1_overflow));
  inc_dec inc_dec_1 (
    .Sub(Control0), .A(A), .Result(inc_dec_1_result), .Carry(inc_dec_1_carry), .Overflow(inc_dec_1_overflow));
  Rotate_Left_Right rotate_left_right_1 (.A(A), .Result(rotate_left_right_1_result), .in_2(Control0));
  Multiplexer #(.select(2), .width(24), .enable("false")) multiplexer_1 (
    .in0(n24_bit_and_or_1_result), .in1(add_sub_1_result), .in2(inc_dec_1_result),
    .in3(rotate_left_right_1_result), .out(Result), .sel({Control2, Control1}));
  _23th_bit_out u_23th_bit_out_1 (.Input(Result), ._23th_bit(Negative));
  or or_1 (Overflow, add_sub_1_overflow, inc_dec_1_overflow);
  or or_2 (Carry, add_sub_1_carry, inc_dec_1_carry);
  _24_bit_reduce_or u_24_bit_reduce_or_1 (.Input(Result), .Output(n24_bit_reduce_or_1_output));
  not not_1 (Zero, n24_bit_reduce_or_1_output);
endmodule

// Rotate-Left
module rotate_left (
  input  [23:0] A,
  output [23:0] result
);


  assign result = {A[22:0], A[23]};
endmodule

// INC_DEC
module inc_dec (
  input  Sub,
  input  [23:0] A,
  output [23:0] Result,
  output Carry,
  output Overflow
);

  wire and_1_out, and_2_out, n23th_bit_out_1__23th_bit, n23th_bit_out_2__23th_bit, n23th_bit_out_3__23th_bit,
       not_1_out, not_2_out, not_3_out;
  wire [23:0] n24_bit_xor_1_result;

  _23th_bit_out u_23th_bit_out_1 (.Input(A), ._23th_bit(n23th_bit_out_1__23th_bit));
  not not_1 (not_1_out, n23th_bit_out_1__23th_bit);
  _23th_bit_out u_23th_bit_out_2 (.Input(24'h1), ._23th_bit(n23th_bit_out_2__23th_bit));
  not not_2 (not_2_out, n23th_bit_out_2__23th_bit);
  _24_bit_xor u_24_bit_xor_1 (.B(24'h1), .Result(n24_bit_xor_1_result), .Control(Sub));
  _24_bit_full_adder_concise u_24_bit_full_adder_concise_1 (
    .A(A), .Result(Result), .Carry_in(Sub), .B(n24_bit_xor_1_result), .Carry(Carry));
  _23th_bit_out u_23th_bit_out_3 (.Input(Result), ._23th_bit(n23th_bit_out_3__23th_bit));
  not not_3 (not_3_out, n23th_bit_out_3__23th_bit);
  and and_1 (and_1_out, not_3_out, n23th_bit_out_2__23th_bit, n23th_bit_out_1__23th_bit);
  and and_2 (and_2_out, n23th_bit_out_3__23th_bit, not_2_out, not_1_out);
  or or_1 (Overflow, and_1_out, and_2_out);

  // Notes on the sheet:
  //   A31
  //   B31
  //   Result 31
endmodule

module rotate_right (
  input  [23:0] A,
  output [23:0] result
);


  assign result = {A[0], A[23:1]};
endmodule

// AND_OR
module _24_bit_and_or (
  input  [23:0] A,
  input  [23:0] B,
  input  in_3,
  output [23:0] Result
);

  wire [23:0] n24_bit_and_1_result, n24_bit_or_1_result;

  _24_bit_and u_24_bit_and_1 (.A(A), .Result(n24_bit_and_1_result), .B(B));
  _24_bit_OR u_24_bit_or_1 (.A(A), .Result(n24_bit_or_1_result), .B(B));
  Multiplexer #(.width(24), .enable("false")) multiplexer_1 (
    .in0(n24_bit_and_1_result), .in1(n24_bit_or_1_result), .out(Result), .sel(in_3));
endmodule

// Rotate_Left/Right
module Rotate_Left_Right (
  input  [23:0] A,
  input  in_2,
  output [23:0] Result
);

  wire [23:0] rotate_left_1_result, rotate_right_1_result;

  rotate_left rotate_left_1 (.A(A), .result(rotate_left_1_result));
  rotate_right rotate_right_1 (.A(A), .result(rotate_right_1_result));
  Multiplexer #(.width(24), .enable("false")) multiplexer_1 (
    .in0(rotate_left_1_result), .in1(rotate_right_1_result), .out(Result), .sel(in_2));
endmodule
