// Logisim project BUS-24Bit (1).circ as structural Verilog: 2 circuits, main circuit main
module main (
  input  RESET
);

  wire Clock_out, control_rom_1_ld_a, control_rom_1_ld_b, control_rom_1_ld_c, control_rom_1_ld_d,
       control_rom_1_oe_a, control_rom_1_oe_b, control_rom_1_oe_c, control_rom_1_oe_d, control_rom_1_oe_zero;
  wire [23:0] A_q, B_q, C_q, controlled_buffer_1_out, D_q, E_q;

  Register #(.width(24)) A (
    .D(controlled_buffer_1_out), .en(control_rom_1_ld_a), .Q(A_q), .clk(Clock_out));  // open: clr
  assign controlled_buffer_1_out = control_rom_1_oe_zero ? {24{1'b0}} : 24'bz;  // Controlled_Buffer controlled_buffer_1
  assign controlled_buffer_1_out = control_rom_1_oe_a ? A_q : 24'bz;  // Controlled_Buffer controlled_buffer_2
  Register #(.width(24)) B (
    .D(controlled_buffer_1_out), .en(control_rom_1_ld_b), .Q(B_q), .clk(Clock_out));  // open: clr
  assign controlled_buffer_1_out = control_rom_1_oe_b ? B_q : 24'bz;  // Controlled_Buffer controlled_buffer_3
  Register #(.width(24)) C (
    .D(controlled_buffer_1_out), .en(control_rom_1_ld_c), .Q(C_q), .clk(Clock_out));  // open: clr
  Control_ROM control_rom_1 (
    .CLK(Clock_out), .Reset(RESET), .LD_D(control_rom_1_ld_d), .LD_B(control_rom_1_ld_b),
    .LD_C(control_rom_1_ld_c), .LD_A(control_rom_1_ld_a), .OE_D(control_rom_1_oe_d),
    .OE_B(control_rom_1_oe_b), .OE_C(control_rom_1_oe_c), .OE_A(control_rom_1_oe_a),
    .OE_ZERO(control_rom_1_oe_zero));
  Register #(.width(24)) D (
    .D(controlled_buffer_1_out), .en(control_rom_1_ld_d), .Q(D_q), .clk(Clock_out));  // open: clr
  assign controlled_buffer_1_out = control_rom_1_oe_c ? C_q : 24'bz;  // Controlled_Buffer controlled_buffer_4
  Clock Clock (.out(Clock_out));
  assign controlled_buffer_1_out = control_rom_1_oe_d ? D_q : 24'bz;  // Controlled_Buffer controlled_buffer_5
  Register #(.width(24)) E (.D(controlled_buffer_1_out), .en(1'b0), .Q(E_q), .clk(Clock_out));  // open: clr
  assign controlled_buffer_1_out = 1'b0 ? E_q : 24'bz;  // Controlled_Buffer controlled_buffer_6
endmodule

// Control ROM
module Control_ROM (
  input  CLK,
  input  Reset,
  output LD_D,
  output LD_B,
  output LD_C,
  output LD_A,
  output OE_D,
  output OE_B,
  output OE_C,
  output OE_A,
  output OE_ZERO
);

  wire [2:0] counter_1_q;

  Counter #(.width(3), .max('h7)) counter_1 (.Q(counter_1_q), .clk(CLK), .clr(Reset));  // open: load, D, count, carry
  ROM #(.addrWidth(3), .dataWidth(9)) rom_1 (
    .addr(counter_1_q), .data({OE_ZERO, OE_A, OE_C, OE_B, OE_D, LD_A, LD_C, LD_B, LD_D}));  // open: sel

  // Notes on the sheet:
  //   contents of rom_1 (hex, n*v repeats v):
  //   14 101 48 104 82 108 24 102
endmodule
